# Fritzing sketch circuit (saved by Fritzing 0.9.3b)

parts:
  Digispark1 = Digispark
  M1 = fc-51 [package=THT]
  U1 = L9110 H-bridge module [part_number="L9110 H-bridge"]
  BATT1 = 3xAAA Switchable Battery Pack w/Bare Wire
  M2 = DC Motor
  M3 = DC Motor

nets:
  N1: Digispark1.P0, U1.A-IB
  N2: Digispark1.P1, U1.A-IA
  N3: Digispark1.P2, U1.B-IA
  N4: Digispark1.P3, U1.B-IB
  N5: Digispark1.P4, M1.pin1
  N6: M1.pin2, U1.GND, BATT1.NEG
  N7: U1.VCC, BATT1.POS
  N8: U1.MOTOR_A-A, M3.pin_2
  N9: U1.MOTOR_A-B, M3.pin_1
  N10: U1.MOTOR_B-A, M2.pin_2
  N11: U1.MOTOR_B-B, M2.pin_1

notes:
  Black == GND
  Red == 5V
  Both supplied from 5V power source
  AAA Battery pack provides power for motors only!
  Black == GND
  This is a shared GND between all devices and power sources.
  Power can be supplied via the (micro) USB port of the ATtiny85 or via VIN pin.

custom parts:
  Digispark: The Digispark is an Attiny85 based microcontroller development board similar to the Arduino line, only cheaper, smaller, and a bit less powerful. With a whole host of shields to extend its functionality and the ability to use the familiar Arduino IDE the Digispark is a great way to jump into electronics, or perfect for when an Arduino is too big or too much.
  3xAAA Switchable Battery Pack w/Bare Wire: 3xAAA Switchable Battery Pack w/Bare Wire Connectors
